# Fritzing sketch esp8266wifi_cp2102 (saved by Fritzing 0.9.3b)

parts:
  ESP8266_WiFi_Shield1 = ESP8266 WiFi Shield
  USBUART1 = CP2102 USB UART Breakout

nets:
  GND: ESP8266_WiFi_Shield1.GND, USBUART1.GND
  N1: ESP8266_WiFi_Shield1.5V, USBUART1.VCCIO
  N2: ESP8266_WiFi_Shield1.RXD, USBUART1.TXD
  N3: ESP8266_WiFi_Shield1.TXD, USBUART1.RXD

custom parts:
  ESP8266 WiFi Shield: ESP8266 WiFi Shield for the awesome Arduino microcontroller.
  CP2102 USB UART Breakout: CP2102 Usb Uart Breakout Board with Battery
