# Fritzing sketch lora32-leddht22 (saved by Fritzing 0.9.3b)
breadboards: 1

parts:
  DHT22 = DHT22 Humidity and Temperature Sensor
  R3 = Resistor [tolerance=±5% resistance=10k package=THT]
  R2 = Resistor [tolerance=±5% resistance=330 package=THT]
  LED1 = LED - 5mm [color="Red (633nm)" package="5 mm [THT]"]
  Heltec_WiFi_LoRa_32_V2 = Heltec WiFi LoRa 32 V2 [part_number=HTIT-WB32LA]

nets:
  N1: DHT22.VDD, R3.Pin_0
  N2: DHT22.DATA, R3.Pin_1, Heltec_WiFi_LoRa_32_V2.pin_34
  N3: DHT22.GND, R2.Pin_0
  N4: R2.Pin_1, LED1.cathode
  N5: LED1.anode, Heltec_WiFi_LoRa_32_V2.pin_31
  N6: Heltec_WiFi_LoRa_32_V2.pin_16, Heltec_WiFi_LoRa_32_V2.pin_17
  N7: Heltec_WiFi_LoRa_32_V2.pin_18, Heltec_WiFi_LoRa_32_V2.pin_19
  N8: Heltec_WiFi_LoRa_32_V2.pin_21, Heltec_WiFi_LoRa_32_V2.pin_22

custom parts:
  Heltec WiFi LoRa 32 V2: Heltec WiFi LoRa 32 V2 WiFi LoRa 32 is a classic IoT dev-board designed & produced by Heltec Automation(TM). It’s a highly integrated product based on ESP32 + SX127x, it has Wi-Fi, BLE, LoRa functions, also Li-Po battery management system, 0.96″ OLED are also included. It’s the best choice for smart cities, smart farms, smart home, and IoT makers.
