# Fritzing sketch node32s-leddht22 (saved by Fritzing 0.9.3b)
breadboards: 1

parts:
  DHT22 = DHT22 Humidity and Temperature Sensor
  R3 = Resistor [tolerance=±5% resistance=10k package=THT]
  부품1 = node32s
  R2 = Resistor [tolerance=±5% resistance=330 package=THT]
  LED1 = LED - 5mm [color="Red (633nm)" package="5 mm [THT]"]

nets:
  VDD: DHT22.VDD, R3.Pin_0, 부품1.3.3V
  N1: DHT22.DATA, R3.Pin_1, 부품1.IO4
  GND: DHT22.GND, 부품1.GND, R2.Pin_0
  N2: 부품1.IO5, LED1.anode
  N3: R2.Pin_1, LED1.cathode
