# Fritzing sketch esp8266_wifi_shield_dht22 (saved by Fritzing 0.9.3b)
breadboards: 1

parts:
  부품1 = Arduino Uno (Rev3)
  R1 = Resistor [tolerance=±5% resistance=1k package=THT]
  R2 = Resistor [tolerance=±5% resistance=2.2k package=THT]
  DHT1 = DHT22 Humidity and Temperature Sensor
  R6 = Resistor [tolerance=±5% resistance=10k package=THT]
  ESP8266_WiFi_Shield1 = ESP8266 WiFi Shield

nets:
  GND: 부품1.GND, R2.Pin_0, DHT1.GND, ESP8266_WiFi_Shield1.GND
  N1: 부품1.D0/RX, R1.Pin_0
  N2: 부품1.D1/TX, ESP8266_WiFi_Shield1.TXD
  5V: 부품1.5V, DHT1.VDD, R6.Pin_1, ESP8266_WiFi_Shield1.5V
  N3: R1.Pin_1, R2.Pin_1, ESP8266_WiFi_Shield1.RXD
  N4: DHT1.DATA, R6.Pin_0

custom parts:
  ESP8266 WiFi Shield: ESP8266 WiFi Shield for the awesome Arduino microcontroller.
