# Fritzing sketch esp8266wifi_arduino (saved by Fritzing 0.9.3b)

parts:
  ESP8266_WiFi_Shield1 = ESP8266 WiFi Shield
  부품1 = Arduino Uno (Rev3)

nets:
  N1: ESP8266_WiFi_Shield1.RXD, 부품1.D0/RX
  N2: ESP8266_WiFi_Shield1.TXD, 부품1.D1/TX
  5V: ESP8266_WiFi_Shield1.5V, 부품1.5V
  GND: ESP8266_WiFi_Shield1.GND, 부품1.GND

custom parts:
  ESP8266 WiFi Shield: ESP8266 WiFi Shield for the awesome Arduino microcontroller.
