# Fritzing sketch node32s-dht22 (saved by Fritzing 0.9.3b)
breadboards: 1

parts:
  DHT22 = DHT22 Humidity and Temperature Sensor
  R1 = Resistor [tolerance=±5% resistance=10k package=THT]
  부품1 = node32s

nets (from the schematic view):
  VDD: DHT22.VDD, R1.Pin_1, 부품1.3.3V
  N1: DHT22.DATA, R1.Pin_0, 부품1.IO4
  GND: DHT22.GND, 부품1.GND
